// Logisim project Circuito.circ as structural Verilog: 1 circuit, main circuit main
module main (
  input  [2:0] in_1,
  input  [2:0] in_2,
  output [2:0] out_3
);

  wire A0_nB1_out, A0B0_out, A1_nA0_out, A1_nB0_out, A1A0_out, A1B1_out, A2_B2_out, A2_nB2_out,
       A2A0_nB1_nB0_out, A2A0_out, A2A0B1B0_out, A2A1_out, A2A1A0_nB2_out, B1_nB0_out, B1B0_out,
       B2B0_nA1_nA0_out, B2B0_out, B2B0A1A0_out, B2B1_out, B2B1B0_nA2_out, nA0B1_out, nA1_nA0_out, nA1B0_out,
       nA2B2_out, nB1_nB0_out, not_1_out, not_2_out, not_3_out, not_4_out, not_5_out, not_6_out;

  not not_1 (not_1_out, in_1[2]);
  not not_2 (not_2_out, in_1[1]);
  not not_3 (not_3_out, in_1[0]);
  not not_4 (not_4_out, in_2[0]);
  not not_5 (not_5_out, in_2[2]);
  not not_6 (not_6_out, in_2[1]);
  and A2_B2 (A2_B2_out, in_1[2], in_2[2]);
  and A2A1 (A2A1_out, in_1[2], in_1[1]);
  and B2B1 (B2B1_out, in_2[2], in_2[1]);
  and B2B0 (B2B0_out, in_2[2], in_2[0]);
  and nA1_nA0 (nA1_nA0_out, not_2_out, not_3_out);
  and nB1_nB0 (nB1_nB0_out, not_6_out, not_4_out);
  and A1A0 (A1A0_out, in_1[1], in_1[0]);
  and A2A0 (A2A0_out, in_1[2], in_1[0]);
  and B1B0 (B1B0_out, in_2[1], in_2[0]);
  and A1B1 (A1B1_out, in_1[1], in_2[1]);
  and nA0B1 (nA0B1_out, in_2[1], not_3_out);
  and A1_nB0 (A1_nB0_out, not_4_out, in_1[1]);
  and A1_nA0 (A1_nA0_out, not_3_out, in_1[1]);
  and B1_nB0 (B1_nB0_out, not_4_out, in_2[1]);
  and nA1B0 (nA1B0_out, not_2_out, in_2[0]);
  and A0_nB1 (A0_nB1_out, in_1[0], not_6_out);
  and A0B0 (A0B0_out, in_2[0], in_1[0]);
  and A2_nB2 (A2_nB2_out, in_1[2], not_5_out);
  and nA2B2 (nA2B2_out, not_1_out, in_2[2]);
  and B2B0A1A0 (B2B0A1A0_out, B2B0_out, A1A0_out);
  and B2B0_nA1_nA0 (B2B0_nA1_nA0_out, B2B0_out, nA1_nA0_out);
  and A2A1A0_nB2 (A2A1A0_nB2_out, A1A0_out, A2_nB2_out);
  and A2A0_nB1_nB0 (A2A0_nB1_nB0_out, A2A0_out, nB1_nB0_out);
  and A2A0B1B0 (A2A0B1B0_out, A2A0_out, B1B0_out);
  and B2B1B0_nA2 (B2B1B0_nA2_out, B1B0_out, nA2B2_out);
  or or_1 (out_3[2], A2_B2_out, A2A1_out, B2B1_out, B2B0_nA1_nA0_out, B2B0A1A0_out, A2A0_nB1_nB0_out, A2A0B1B0_out);
  or or_2 (out_3[1], B2B1_out, A2A1_out, A1B1_out, nA0B1_out, A1_nB0_out, A1_nA0_out, B1_nB0_out);
  or or_3 (out_3[0], nA1B0_out, A0_nB1_out, A0B0_out, A2A1A0_nB2_out, B2B1B0_nA2_out);
endmodule
