// Logisim project CircuitoT2.circ as structural Verilog: 9 circuits, main circuit Ganador
module Ganador (
  input  [2:0] in_1,
  input  [2:0] in_2,
  output [2:0] out_3
);

  wire A0_nB1_out, A0B0_out, A1_nA0_out, A1_nB0_out, A1A0_out, A1B1_out, A2_B2_out, A2_nB2_out,
       A2A0_nB1_nB0_out, A2A0_out, A2A0B1B0_out, A2A1_out, A2A1A0_nB2_out, B1_nB0_out, B1B0_out,
       B2B0_nA1_nA0_out, B2B0_out, B2B0A1A0_out, B2B1_out, B2B1B0_nA2_out, nA0B1_out, nA1_nA0_out, nA1B0_out,
       nA2B2_out, nB1_nB0_out, not_1_out, not_2_out, not_3_out, not_4_out, not_5_out, not_6_out;

  not not_1 (not_1_out, in_1[2]);
  not not_2 (not_2_out, in_1[1]);
  not not_3 (not_3_out, in_1[0]);
  not not_4 (not_4_out, in_2[2]);
  not not_5 (not_5_out, in_2[1]);
  not not_6 (not_6_out, in_2[0]);
  and A2_B2 (A2_B2_out, in_1[2], in_2[2]);
  and A2A1 (A2A1_out, in_1[2], in_1[1]);
  and B2B1 (B2B1_out, in_2[2], in_2[1]);
  and B2B0 (B2B0_out, in_2[2], in_2[0]);
  and nA1_nA0 (nA1_nA0_out, not_2_out, not_3_out);
  and nB1_nB0 (nB1_nB0_out, not_5_out, not_6_out);
  and A1A0 (A1A0_out, in_1[1], in_1[0]);
  and A2A0 (A2A0_out, in_1[2], in_1[0]);
  and B1B0 (B1B0_out, in_2[1], in_2[0]);
  and A1B1 (A1B1_out, in_1[1], in_2[1]);
  and nA0B1 (nA0B1_out, in_2[1], not_3_out);
  and A1_nB0 (A1_nB0_out, not_6_out, in_1[1]);
  and A1_nA0 (A1_nA0_out, not_3_out, in_1[1]);
  and B1_nB0 (B1_nB0_out, not_6_out, in_2[1]);
  and nA1B0 (nA1B0_out, not_2_out, in_2[0]);
  and A0_nB1 (A0_nB1_out, in_1[0], not_5_out);
  and A0B0 (A0B0_out, in_2[0], in_1[0]);
  and A2_nB2 (A2_nB2_out, in_1[2], not_4_out);
  and nA2B2 (nA2B2_out, not_1_out, in_2[2]);
  and B2B0A1A0 (B2B0A1A0_out, B2B0_out, A1A0_out);
  and B2B0_nA1_nA0 (B2B0_nA1_nA0_out, B2B0_out, nA1_nA0_out);
  and A2A1A0_nB2 (A2A1A0_nB2_out, A1A0_out, A2_nB2_out);
  and A2A0_nB1_nB0 (A2A0_nB1_nB0_out, A2A0_out, nB1_nB0_out);
  and A2A0B1B0 (A2A0B1B0_out, A2A0_out, B1B0_out);
  and B2B1B0_nA2 (B2B1B0_nA2_out, B1B0_out, nA2B2_out);
  or or_1 (out_3[2], A2_B2_out, A2A1_out, B2B1_out, B2B0_nA1_nA0_out, B2B0A1A0_out, A2A0_nB1_nB0_out, A2A0B1B0_out);
  or or_2 (out_3[1], B2B1_out, A2A1_out, A1B1_out, nA0B1_out, A1_nB0_out, A1_nA0_out, B1_nB0_out);
  or or_3 (out_3[0], nA1B0_out, A0_nB1_out, A0B0_out, A2A1A0_nB2_out, B2B1B0_nA2_out);
endmodule

module Comp (
  input  in_1,
  input  in_2,
  input  in_3,
  input  in_4,
  input  in_5,
  input  in_6,
  output out_7
);

  wire and_1_out, and_2_out, and_3_out, nor_1_out, nor_2_out, nor_3_out, or_1_out, or_2_out, or_3_out;

  nor nor_1 (nor_1_out, in_6, in_3);
  and and_1 (and_1_out, in_6, in_3);
  nor nor_2 (nor_2_out, in_5, in_2);
  and and_2 (and_2_out, in_5, in_2);
  nor nor_3 (nor_3_out, in_4, in_1);
  and and_3 (and_3_out, in_4, in_1);
  or or_1 (or_1_out, nor_1_out, and_1_out);
  or or_2 (or_2_out, nor_2_out, and_2_out);
  or or_3 (or_3_out, nor_3_out, and_3_out);
  and and_4 (out_7, or_1_out, or_2_out, or_3_out);
endmodule

module main (
  input  Reset,
  input  [2:0] in_2,
  input  [2:0] in_3,
  output [3:0] out_4
);

  wire clock_1_out;
  wire [2:0] flipflopd7bit_1_out_4, ganador_1_out_3;
  wire [3:0] s_3_1_out_2;
  wire [5:4] comp_2_out_7;

  Ganador ganador_1 (.in_1(in_2), .in_2(in_3), .out_3(ganador_1_out_3));
  Comp comp_1 (
    .in_1(in_2[2]), .in_2(in_2[1]), .in_3(in_2[0]), .in_4(ganador_1_out_3[2]), .in_5(ganador_1_out_3[1]),
    .in_6(ganador_1_out_3[0]), .out_7(comp_2_out_7[5]));
  Comp comp_2 (
    .in_1(in_2[2]), .in_2(in_2[1]), .in_3(in_2[0]), .in_4(flipflopd7bit_1_out_4[2]),
    .in_5(flipflopd7bit_1_out_4[1]), .in_6(flipflopd7bit_1_out_4[0]), .out_7(comp_2_out_7[4]));
  S_3 s_3_1 (.in_1({comp_2_out_7, out_4}), .out_2(s_3_1_out_2[0]));
  S_2 s_2_1 (.in_1({comp_2_out_7, out_4[2:0]}), .out_2(s_3_1_out_2[1]));
  S_1 s_1_1 (.in_1({comp_2_out_7, out_4[1:0]}), .out_2(s_3_1_out_2[2]));
  S_0 s_0_1 (.in_1({comp_2_out_7, out_4[0]}), .out_2(s_3_1_out_2[3]));
  Clock clock_1 (.out(clock_1_out));
  FlipFlopD7bit flipflopd7bit_1 (
    .in_1(clock_1_out), .in_2({in_2, s_3_1_out_2}),
    .out_4({flipflopd7bit_1_out_4, out_4[0], out_4[1], out_4[2], out_4[3]}), .in_3(Reset));
endmodule

module S_3 (
  input  [5:0] in_1,
  output out_2
);

  wire and_1_out, xor_1_out;

  and and_1 (and_1_out, in_1[5], in_1[2], in_1[1], in_1[0]);
  and and_2 (out_2, in_1[4], xor_1_out);
  xor xor_1 (xor_1_out, in_1[3], and_1_out);
endmodule

module S_0 (
  input  [2:0] in_1,
  output out_2
);

  wire and_1_out;

  and and_1 (and_1_out, in_1[1], in_1[0]);
  xor xor_1 (out_2, in_1[2], and_1_out);
endmodule

module S_2 (
  input  [4:0] in_1,
  output out_2
);

  wire and_1_out, xor_1_out;

  and and_1 (and_1_out, in_1[4], in_1[1], in_1[0]);
  xor xor_1 (xor_1_out, in_1[2], and_1_out);
  and and_2 (out_2, in_1[3], xor_1_out);
endmodule

module S_1 (
  input  [3:0] in_1,
  output out_2
);

  wire and_1_out, xor_1_out;

  xor xor_1 (xor_1_out, in_1[1], and_1_out);
  and and_1 (and_1_out, in_1[3], in_1[0]);
  and and_2 (out_2, in_1[2], xor_1_out);
endmodule

module FlipFlopD (
  input  in_1,
  input  in_2,
  input  in_3,
  output out_4,
  output out_5
);

  wire nand_1_out, nand_2_out, nand_3_out, nand_4_out, nand_5_out, nand_6_out, nand_7_out, not_1_out;

  nand nand_1 (nand_1_out, in_1, in_1);
  nand nand_2 (nand_2_out, in_1, in_2);
  nand nand_3 (nand_3_out, in_2, nand_1_out);
  nand nand_4 (nand_4_out, nand_2_out, nand_5_out);
  nand nand_5 (nand_5_out, nand_4_out, in_3, nand_3_out);
  not not_1 (not_1_out, in_2);
  nand nand_6 (nand_6_out, nand_4_out, not_1_out);
  nand nand_7 (nand_7_out, not_1_out, nand_5_out);
  nand nand_8 (out_4, nand_6_out, out_5);
  nand nand_9 (out_5, out_4, nand_7_out);
endmodule

module FlipFlopD7bit (
  input  in_1,
  input  [6:0] in_2,
  input  in_3,
  output [6:0] out_4
);

  FlipFlopD flipflopd_1 (.in_1(in_2[0]), .in_2(in_1), .in_3(in_3), .out_4(out_4[0]));  // open: out_5
  FlipFlopD flipflopd_2 (.in_1(in_2[1]), .in_2(in_1), .in_3(in_3), .out_4(out_4[1]));  // open: out_5
  FlipFlopD flipflopd_3 (.in_1(in_2[2]), .in_2(in_1), .in_3(in_3), .out_4(out_4[2]));  // open: out_5
  FlipFlopD flipflopd_4 (.in_1(in_2[3]), .in_2(in_1), .in_3(in_3), .out_4(out_4[3]));  // open: out_5
  FlipFlopD flipflopd_5 (.in_1(in_2[4]), .in_2(in_1), .in_3(in_3), .out_4(out_4[4]));  // open: out_5
  FlipFlopD flipflopd_6 (.in_1(in_2[5]), .in_2(in_1), .in_3(in_3), .out_4(out_4[5]));  // open: out_5
  FlipFlopD flipflopd_7 (.in_1(in_2[6]), .in_2(in_1), .in_3(in_3), .out_4(out_4[6]));  // open: out_5
endmodule
