// Logisim project Comparador_num3bits.circ as structural Verilog: 1 circuit, main circuit main
module main (
  input  in_1,
  input  in_2,
  input  in_3,
  input  in_4,
  input  in_5,
  input  in_6,
  output out_7
);

  wire and_1_out, and_2_out, and_3_out, nor_1_out, nor_2_out, nor_3_out, or_1_out, or_2_out, or_3_out;

  nor nor_1 (nor_1_out, in_6, in_3);
  and and_1 (and_1_out, in_6, in_3);
  nor nor_2 (nor_2_out, in_5, in_2);
  and and_2 (and_2_out, in_5, in_2);
  nor nor_3 (nor_3_out, in_4, in_1);
  and and_3 (and_3_out, in_4, in_1);
  or or_1 (or_1_out, nor_1_out, and_1_out);
  or or_2 (or_2_out, nor_2_out, and_2_out);
  or or_3 (or_3_out, nor_3_out, and_3_out);
  and and_4 (out_7, or_1_out, or_2_out, or_3_out);
endmodule
